# Fritzing sketch schematic (saved by Fritzing 0.9.2b)
breadboards: 1

parts:
  Left_stern = Basic Servo
  Rudder = Basic Servo
  Right_stern = Basic Servo
  Part4 = IR Receiver Breakout [package=PCB]
  Proppeler = DC Motor
  R1 = Resistor [tolerance=±5% resistance=220 package="2512 [SMD]"]
  R2 = Resistor [tolerance=±5% resistance=220 package="2512 [SMD]"]
  R3 = Resistor [tolerance=±5% resistance=220 package="2512 [SMD]"]
  Part3 = Motor Driver 1A Dual TB6612FNG
  Board_source = DC Power [voltage=5V]
  Propulsion_source = DC Power [voltage=6V]
  Servomotors_source = DC Power [voltage=6V]
  Part1 = Arduino Nano (Rev3.0)
  LED1 = RGB LED - (4 legs) [package="5 mm [THT]"]

nets:
  GND: Left_stern.gnd, Rudder.gnd, Right_stern.gnd, Servomotors_source.V-
  VCC: Left_stern.vcc, Rudder.vcc, Right_stern.vcc, Servomotors_source.V+
  N1: Left_stern.pulse, Part1.D5
  N2: Rudder.pulse, Part1.D7
  N3: Right_stern.pulse, Part1.D6
  GND_2: Part4.GND, Board_source.V-, Part1.GND
  N4: Part4.OUT, Part1.D10
  VCC_2: Part4.VCC, Part1.5V
  N5: Proppeler.pin_1, Part3.A01
  N6: Proppeler.pin_2, Part3.A02
  N7: R1.Pin_0, Part1.D4
  N8: R1.Pin_1, LED1.blue_cathode
  N9: R2.Pin_0, Part1.D3
  N10: R2.Pin_1, LED1.green_cathode
  N11: R3.Pin_0, Part1.D2
  N12: R3.Pin_1, LED1.red_cathode
  N13: Part3.GND, Propulsion_source.V-
  N14: Part3.VCC, Propulsion_source.V+
  N15: Part3.AIN2, Part1.D9
  N16: Part3.AIN1, Part1.D8
  N17: Board_source.V+, Part1.VIN
  N18: Part1.3V3, LED1.common_anode
