# Fritzing sketch submarine (saved by Fritzing 0.9.3b)
breadboards: 1

parts:
  Driver = L9110 H-bridge module [part_number="L9110 H-bridge"]
  IR_receiver = IR Receiver Breakout [part_number="Move Command" package=PCB]
  6_0_V = Battery Holders [package=battery-aa]
  Motor_controller = Arduino Nano (Rev3.0)
  6_0_V_2 = Battery Holders [package=battery-aa]
  6_0_V_3 = Battery Holders [package=battery-aa]
  Front_hydroplanes = Basic Servo
  Back_hydroplanes = Basic Servo
  6_0_V_4 = Battery Holders [package=battery-aa]
  Rudders = Basic Servo
  5_6_V = Battery Holders [package=battery-aa]
  U2 = MPU 9250 Breakout [package="SIP (Single Inline) [THT]"]
  Morse_LED = RGB LED (com. cathode, rgb) [package="5 mm [THT]"]
  3_3_V = Resistor [tolerance=±5% resistance=220 package=THT]
  Blue = Resistor [tolerance=±5% resistance=220 package=THT]
  Red = Resistor [tolerance=±5% resistance=220 package=THT]
  HPCB_380_1_6V = DC Motor with two-phase hall-encoder [part_number="Pololu DC Encoder"]
  Back = Humidity Sensor - HIH-4030 Breakout
  Green = Resistor [tolerance=±5% resistance=220 package=THT]
  Driver1 = L9110 H-bridge module [part_number="L9110 H-bridge"]
  6_0_V_5 = Battery Holders [package=battery-aa]
  Front = DC Motor [part_number="HPCB 250:1 6V1"]
  Front_2 = Humidity Sensor - HIH-4030 Breakout
  Ballast = Humidity Sensor - HIH-4030 Breakout

nets:
  N1: Driver.GND, 6_0_V.-
  N2: Driver.VCC, 6_0_V.+
  N3: Driver.A-IA, Motor_controller.D8
  N4: Driver.A-IB, Motor_controller.D7
  N5: Driver.MOTOR_A-A, HPCB_380_1_6V.pin1
  N6: Driver.MOTOR_A-B, HPCB_380_1_6V.pin6
  GND: IR_receiver.GND, Motor_controller.GND, 5_6_V.-, U2.GND, HPCB_380_1_6V.pin5, Back.GND, Front_2.GND, Ballast.GND
  N7: IR_receiver.OUT, Motor_controller.D11/MOSI
  VCC: IR_receiver.VCC, Motor_controller.5V
  N8: Motor_controller.D2, Driver1.B-IA
  N9: Motor_controller.D3, Rudders.pulse
  N10: Motor_controller.D4, Driver1.B-IB
  N11: Motor_controller.D5, Back_hydroplanes.pulse
  N12: Motor_controller.D6, Front_hydroplanes.pulse
  N13: Motor_controller.D9, HPCB_380_1_6V.pin3
  N14: Motor_controller.D10, HPCB_380_1_6V.pin4
  N15: Motor_controller.VIN, 5_6_V.+
  N16: Motor_controller.A5, U2.SCL
  N17: Motor_controller.A4, U2.SDA
  N18: Motor_controller.A3, Blue.Pin_1
  N19: Motor_controller.A2, Green.Pin_1
  N20: Motor_controller.A1, Red.Pin_1
  N21: Motor_controller.A0, Back.OUT, Front_2.OUT, Ballast.OUT
  VCC_2: Motor_controller.3V3, U2.VCC, 3_3_V.Pin_1, HPCB_380_1_6V.pin2, Back.VCC, Front_2.VCC, Ballast.VCC
  N22: 6_0_V_2.-, Back_hydroplanes.gnd
  N23: 6_0_V_2.+, Back_hydroplanes.vcc
  N24: 6_0_V_3.-, Front_hydroplanes.gnd
  N25: 6_0_V_3.+, Front_hydroplanes.vcc
  N26: 6_0_V_4.-, Rudders.gnd
  N27: 6_0_V_4.+, Rudders.vcc
  N28: Morse_LED.red_anode, Blue.Pin_0
  N29: Morse_LED.common_cathode, 3_3_V.Pin_0
  N30: Morse_LED.green_anode, Green.Pin_0
  N31: Morse_LED.blue_anode, Red.Pin_0
  N32: Driver1.GND, 6_0_V_5.-
  N33: Driver1.VCC, 6_0_V_5.+
  N34: Driver1.MOTOR_B-A, Front.pin_2
  N35: Driver1.MOTOR_B-B, Front.pin_1

notes:
  Wings
  Communications
  Metere Class - Submarine drone, 1
  Command
  Propeller
  Ballast

custom parts:
  MPU 9250 Breakout: Generic MPU 9250 Breakout Board
