# Fritzing sketch submarine (saved by Fritzing 0.9.2b)
breadboards: 1

parts:
  Propulsion = DC Motor [part_number="HPCB 6V 50:1"]
  Dive_planes_front = Basic Servo [part_number=MG996R]
  Antenna_module_of_communication = 2.4GHz Low Power Transceiver [package=qfn20]
  Sensor_of_humidity_front = HIH-4030 [package=hih-4030]
  IMU_front = gy9250
  Sensor_of_sonar_left = SRF05 Ultrasonic Rangefinder
  Sensor_of_sonar_right = SRF05 Ultrasonic Rangefinder
  Actions_board = Arduino Nano (Rev3.0)
  Sensor_of_humidity_ballast = HIH-4030 [package=hih-4030]
  Sensor_of_humidity_back = HIH-4030 [package=hih-4030]
  Light_Morse_signal = RGB LED - (4 legs) [package="5 mm [THT]"]
  Battery_1 = Battery Holders [part_number=6V package=battery-aa]
  Q1 = npn-Powertransistor [part_number="BD 241 C" package="TO220 [THT]"]
  R1 = Resistor [tolerance=±5% resistance=1k package=THT]
  Dive_planes_back = Basic Servo [part_number=MG996R]
  Battery_2 = Battery Holders [part_number=6V package=battery-aa]
  Q2 = npn-Powertransistor [part_number="BD 241 C" package="TO220 [THT]"]
  R2 = Resistor [tolerance=±5% resistance=1k package=THT]
  Rudders = Basic Servo [part_number=MG996R]
  Battery_3 = Battery Holders [part_number=6V package=battery-aa]
  Q3 = npn-Powertransistor [part_number="BD 241 C" package="TO220 [THT]"]
  R3 = Resistor [tolerance=±5% resistance=1k package=THT]
  Antenna_rise_system = Basic Servo [part_number=MG996R]
  Battery_4 = Battery Holders [part_number=6V package=battery-aa]
  Q4 = npn-Powertransistor [part_number="BD 241 C" package="TO220 [THT]"]
  R5 = Resistor [tolerance=±5% resistance=1k package=THT]
  Sonar_rotation_system = Basic Servo [part_number=ES08MA]
  Battery_5 = Battery Holders [part_number=6V package=battery-aa]
  Q5 = npn-Powertransistor [part_number="BD 241 C" package="TO220 [THT]"]
  R6 = Resistor [tolerance=±5% resistance=1k package=THT]
  Battery_6 = Battery Holders [part_number=6V package=battery-aa]
  R7 = Resistor [tolerance=±5% resistance=1k package=THT]
  R8 = Resistor [tolerance=±5% resistance=1k package=THT]
  R9 = Resistor [tolerance=±5% resistance=1k package=THT]
  R10 = Resistor [tolerance=±5% resistance=1k package=THT]
  R11 = Resistor [tolerance=±5% resistance=220 package=THT]
  R12 = Resistor [tolerance=±5% resistance=220 package=THT]
  R13 = Resistor [tolerance=±5% resistance=220 package=THT]
  R14 = Resistor [tolerance=±5% resistance=220 package=THT]
  D1 = Rectifier Diode [part_number=1N5402 package="300 mil [THT]"]
  Q6 = npn-Powertransistor [part_number="BD 241 C" package="TO220 [THT]"]
  D2 = Rectifier Diode [part_number=1N5402 package="300 mil [THT]"]
  D3 = Rectifier Diode [part_number=1N5402 package="300 mil [THT]"]
  D4 = Rectifier Diode [part_number=1N5402 package="300 mil [THT]"]
  D5 = Rectifier Diode [part_number=1N5402 package="300 mil [THT]"]
  Q7 = pnp-Powertransistor [part_number="BD 244 CG" package="TO220 [THT]"]
  C1 = Ceramic Capacitor [capacitance=10nF voltage=20V package="100 mil [THT, multilayer]"]
  Q8 = pnp-Powertransistor [part_number="BD 244 CG" package="TO220 [THT]"]
  Q9 = npn-Powertransistor [part_number="BD 241 C" package="TO220 [THT]"]
  D6 = Rectifier Diode [part_number=1N5402 package="300 mil [THT]"]
  D7 = Rectifier Diode [part_number=1N5402 package="300 mil [THT]"]
  Q10 = npn-Powertransistor [part_number="BD 241 C" package="TO220 [THT]"]
  Q11 = npn-Powertransistor [part_number="BD 241 C" package="TO220 [THT]"]
  Q12 = npn-Powertransistor [part_number="BD 241 C" package="TO220 [THT]"]
  Communications_board = Arduino Nano (Rev3.0)
  Antenna_raise = POT [package=pot_mammoth]
  Propulsion_2 = POT [package=pot_mammoth]
  Rudders_2 = POT [package=pot_mammoth]
  Hydroplanes = POT [package=pot_mammoth]
  R15 = Resistor [tolerance=±5% resistance=1 package=THT]
  R16 = Resistor [tolerance=±5% resistance=1 package=THT]
  R17 = Resistor [tolerance=±5% resistance=1 package=THT]
  R18 = Resistor [tolerance=±5% resistance=1 package=THT]
  Sonar_sound_speed = SWITCH-MOMENTARY-2 [package=tactile_switch_tall]
  On/Off_sonar = Pushbutton [package="[THT]"]
  Remote_board = Arduino Nano (Rev3.0)
  Antenna_module_of_remote = 2.4GHz Low Power Transceiver [package=qfn20]
  R19 = Resistor [tolerance=±5% resistance=1k package=THT]
  R20 = Resistor [tolerance=±5% resistance=1k package=THT]
  R21 = Resistor [tolerance=±5% resistance=1k package=THT]
  R22 = Resistor [tolerance=±5% resistance=1k package=THT]
  R23 = Resistor [tolerance=±5% resistance=100 package=THT]
  R24 = Resistor [tolerance=±5% resistance=100 package=THT]
  R25 = Resistor [tolerance=±5% resistance=100 package=THT]
  R26 = Resistor [tolerance=±5% resistance=100 package=THT]
  R27 = Resistor [tolerance=±5% resistance=100 package=THT]
  R28 = Resistor [tolerance=±5% resistance=100 package=THT]
  R29 = Resistor [tolerance=±5% resistance=100 package=THT]
  R30 = Resistor [tolerance=±5% resistance=100 package=THT]
  R31 = Resistor [tolerance=±5% resistance=100 package=THT]
  Sensor_of_sonar_front = SRF05 Ultrasonic Rangefinder

nets:
  N1: Propulsion.pin_1, Q7.emitter, C1.0, D7.cathode
  N2: Propulsion.pin_2, C1.1, Q8.emitter, D6.cathode
  N3: Dive_planes_front.gnd, Battery_1.-
  N4: Dive_planes_front.vcc, Q1.emitter
  Actions D5: Dive_planes_front.pulse, Actions_board.D5
  Communications D9: Antenna_module_of_communication.CE, Communications_board.D9
  Communications D8: Antenna_module_of_communication.CSN, Communications_board.D8
  Communications D13: Antenna_module_of_communication.SCK, Communications_board.D13/SCK
  Communications D11: Antenna_module_of_communication.MOSI, Communications_board.D11/MOSI
  Communications D12: Antenna_module_of_communication.MISO, Communications_board.D12/MISO
  Communications D2: Antenna_module_of_communication.IRQ, Communications_board.D2
  N5: Antenna_module_of_communication.VDD, R26.Pin_0
  Communications GND: Sensor_of_humidity_front.GND, IMU_front.pin2, Sensor_of_sonar_left.GND, Sensor_of_sonar_right.GND, Sensor_of_humidity_ballast.GND, Sensor_of_humidity_back.GND, Communications_board.GND, Sensor_of_sonar_front.GND
  Communications A2: Sensor_of_humidity_front.OUT, Communications_board.A2
  N6: Sensor_of_humidity_front.VCC, R25.Pin_1
  N7: IMU_front.pin1, R29.Pin_1
  Communications A5: IMU_front.pin3, Communications_board.A5
  Communications A4: IMU_front.pin4, Communications_board.A4
  N8: Sensor_of_sonar_left.VCC, R27.Pin_1
  Communications D5: Sensor_of_sonar_left.Trig, Communications_board.D5
  Communications A6: Sensor_of_sonar_left.Echo, Communications_board.A6
  N9: Sensor_of_sonar_right.VCC, R28.Pin_1
  Communications D6: Sensor_of_sonar_right.Trig, Communications_board.D6
  Communications A7: Sensor_of_sonar_right.Echo, Communications_board.A7
  Serial 1: Actions_board.D1/TX, Communications_board.D1/TX
  Serial 0: Actions_board.D0/RX, Communications_board.D0/RX
  Actions GND: Actions_board.GND
  Actions D2: Actions_board.D2, R9.Pin_0, R10.Pin_0
  Actions D3: Actions_board.D3, R7.Pin_1, R8.Pin_1
  Actions D4: Actions_board.D4, R1.Pin_0
  Actions D6: Actions_board.D6, Dive_planes_back.pulse
  Actions D7: Actions_board.D7, R2.Pin_0
  Actions D8: Actions_board.D8, R3.Pin_0
  Actions D9: Actions_board.D9, Rudders.pulse
  Actions D10: Actions_board.D10, Antenna_rise_system.pulse
  Actions D11: Actions_board.D11/MOSI, Sonar_rotation_system.pulse
  Actions D12: Actions_board.D12/MISO, R5.Pin_0
  Actions VIN: Actions_board.VIN
  Actions 5.0V: Actions_board.5V, R11.Pin_0, R12.Pin_0, R13.Pin_0, R14.Pin_0
  Actions A7: Actions_board.A7
  Actions A6: Actions_board.A6
  Actions A5: Actions_board.A5
  Actions A4: Actions_board.A4
  Actions A3: Actions_board.A3
  Actions A2: Actions_board.A2, R20.Pin_1
  Actions A1: Actions_board.A1, R21.Pin_0
  Actions A0: Actions_board.A0, R22.Pin_0
  Actions 3.3V: Actions_board.3V3
  Actions D13: Actions_board.D13/SCK, R6.Pin_0
  Communications A0: Sensor_of_humidity_ballast.OUT, Communications_board.A0
  N10: Sensor_of_humidity_ballast.VCC, R23.Pin_1
  Communications A1: Sensor_of_humidity_back.OUT, Communications_board.A1
  N11: Sensor_of_humidity_back.VCC, R24.Pin_1
  N12: Light_Morse_signal.red_cathode, D3.cathode
  N13: Light_Morse_signal.common_anode, R14.Pin_1
  N14: Light_Morse_signal.green_cathode, D2.cathode
  N15: Light_Morse_signal.blue_cathode, D1.cathode
  N16: Battery_1.+, Q1.collector
  N17: Q1.base, R1.Pin_1
  N18: Dive_planes_back.gnd, Battery_2.-
  N19: Dive_planes_back.vcc, Q2.emitter
  N20: Battery_2.+, Q2.collector
  N21: Q2.base, R2.Pin_1
  N22: Rudders.gnd, Battery_3.-
  N23: Rudders.vcc, Q3.emitter
  N24: Battery_3.+, Q3.collector
  N25: Q3.base, R3.Pin_1
  N26: Antenna_rise_system.gnd, Battery_4.-
  N27: Antenna_rise_system.vcc, Q4.emitter
  N28: Battery_4.+, Q4.collector
  N29: Q4.base, R5.Pin_1
  N30: Sonar_rotation_system.gnd, Battery_5.-
  N31: Sonar_rotation_system.vcc, Q5.emitter
  N32: Battery_5.+, Q5.collector
  N33: Q5.base, R6.Pin_1
  N34: Battery_6.-, D4.cathode, D5.cathode
  N35: Battery_6.+, Q6.collector, Q9.collector
  N36: R7.Pin_0, Q9.base
  N37: R8.Pin_0, Q8.base
  N38: R9.Pin_1, Q6.base
  N39: R10.Pin_1, Q7.base
  N40: R11.Pin_1, Q10.collector
  N41: R12.Pin_1, Q12.collector
  N42: R13.Pin_1, Q11.collector
  N43: D1.anode, Q12.emitter
  N44: Q6.emitter, D7.anode
  N45: D2.anode, Q11.emitter
  N46: D3.anode, Q10.emitter
  N47: D4.anode, Q7.collector
  N48: D5.anode, Q8.collector
  N49: Q9.emitter, D6.anode
  N50: Q10.base, R20.Pin_0
  N51: Q11.base, R21.Pin_1
  N52: Q12.base, R22.Pin_1
  Communications D3: Communications_board.D3
  Communications D4: Communications_board.D4
  Communications D7: Communications_board.D7, Sensor_of_sonar_front.Trig
  Communications D10: Communications_board.D10
  Communications VIN: Communications_board.VIN
  Communications 5.0V: Communications_board.5V, R23.Pin_0, R24.Pin_0, R25.Pin_0, R27.Pin_0, R28.Pin_0, R31.Pin_0
  Communications A3: Communications_board.A3, Sensor_of_sonar_front.Echo
  Communications 3.3V: Communications_board.3V3, R26.Pin_1, R29.Pin_0
  Remote A3: Antenna_raise.S, Remote_board.A3
  Remote GND: Antenna_raise.A, Propulsion_2.A, Rudders_2.A, Hydroplanes.A, Remote_board.GND, R19.Pin_1
  N53: Antenna_raise.E, R18.Pin_1
  Remote A0: Propulsion_2.S, Remote_board.A0
  N54: Propulsion_2.E, R15.Pin_1
  Remote A1: Rudders_2.S, Remote_board.A1
  N55: Rudders_2.E, R16.Pin_1
  Remote A2: Hydroplanes.S, Remote_board.A2
  N56: Hydroplanes.E, R17.Pin_1
  Remote 5.0V: R15.Pin_0, R16.Pin_0, R17.Pin_0, R18.Pin_0, On/Off_sonar.Pin_3, On/Off_sonar.Pin_4, Remote_board.5V
  Remote D6: Sonar_sound_speed.2, Remote_board.D6
  Remote D5: Sonar_sound_speed.1, Remote_board.D5
  Remote D4: On/Off_sonar.Pin_1, On/Off_sonar.Pin_2, Remote_board.D4, R19.Pin_0
  Remote 1: Remote_board.D1/TX
  Remote 0: Remote_board.D0/RX
  Remote D2: Remote_board.D2, Antenna_module_of_remote.IRQ
  Remote D3: Remote_board.D3
  Remote D7: Remote_board.D7
  Remote D8: Remote_board.D8, Antenna_module_of_remote.CSN
  Remote D9: Remote_board.D9, Antenna_module_of_remote.CE
  Remote D10: Remote_board.D10
  Remote D11: Remote_board.D11/MOSI, Antenna_module_of_remote.MOSI
  Remote D12: Remote_board.D12/MISO, Antenna_module_of_remote.MISO
  Remote VIN: Remote_board.VIN
  Remote A7: Remote_board.A7
  Remote A6: Remote_board.A6
  Remote A5: Remote_board.A5
  Remote A4: Remote_board.A4
  Remote 3.3V: Remote_board.3V3, R30.Pin_1
  Remote D13: Remote_board.D13/SCK, Antenna_module_of_remote.SCK
  N57: Antenna_module_of_remote.VDD, R30.Pin_0
  N58: R31.Pin_1, Sensor_of_sonar_front.VCC

notes:
  Metere class drone submarine, 5

custom parts:
  gy9250: MPU-9250 module (three-axis gyroscope + three-axis acceleration + three-axis magnetic field). The generic model from ebay et. al. rather than the Sparkfun version.
