# Fritzing sketch schematic (saved by Fritzing 0.9.2b)
breadboards: 1

parts:
  Left_stern = Basic Servo
  Rudder = Basic Servo
  Right_stern = Basic Servo
  Part4 = IR Receiver Breakout [package=PCB]
  Proppeler = DC Motor
  LED1 = RGB LED (com. anode, rbg) [package="5 mm [THT]"]
  R1 = Resistor [tolerance=±5% resistance=220 package="2512 [SMD]"]
  R2 = Resistor [tolerance=±5% resistance=220 package="2512 [SMD]"]
  R3 = Resistor [tolerance=±5% resistance=220 package="2512 [SMD]"]
  Part3 = Motor Driver 1A Dual TB6612FNG
  Board_source = DC Power [voltage=9V]
  Propulsion_source = DC Power [voltage=6V]
  Servomotors_source = DC Power [voltage=6V]
  Part1 = Arduino Uno (Rev3)

nets:
  GND: Left_stern.gnd, Rudder.gnd, Right_stern.gnd, Servomotors_source.V-
  VCC: Left_stern.vcc, Rudder.vcc, Right_stern.vcc, Servomotors_source.V+
  N1: Left_stern.pulse, Part1.D5_PWM
  N2: Rudder.pulse, Part1.D7
  N3: Right_stern.pulse, Part1.D6_PWM
  N4: Part4.GND, Board_source.V-
  N5: Part4.OUT, Part1.D10_PWM/SS
  VCC_2: Part4.VCC, Part1.5V
  N6: Proppeler.pin_1, Part3.A01
  N7: Proppeler.pin_2, Part3.A02
  N8: LED1.red_cathode, R3.Pin_1
  N9: LED1.common_anode, Part1.3V3
  N10: LED1.blue_cathode, R1.Pin_1
  N11: LED1.green_cathode, R2.Pin_1
  N12: R1.Pin_0, Part1.D4
  N13: R2.Pin_0, Part1.D3_PWM
  N14: R3.Pin_0, Part1.D2
  N15: Part3.GND, Propulsion_source.V-
  N16: Part3.VCC, Propulsion_source.V+
  N17: Part3.AIN2, Part1.D9_PWM
  N18: Part3.AIN1, Part1.D8
  N19: Board_source.V+, Part1.VIN
